// Logisim project LC3-2200a.circ as structural Verilog: 4 circuits, main circuit Datapath
module Datapath (
  output [3:0] out_1
);

  wire and_1_out, and_2_out, and_3_out, CLK, DrALU, DrMEM, DrOFF, DrPC, DrREG, EnInt, IE, INT, IntAck,
       Interrupt, IntOut, LdA, LdB, LdCC, LdEnInt, LdIR, LdMAR, LdPC, N, or_1_out, P, Start, WrMEM, WrREG, Z;
  wire [1:0] func;
  wire [2:0] comparator_1_gt;
  wire [3:0] regno;
  wire [23:0] register_3_q;
  wire [27:0] IR;
  wire [31:0] alu_1_out_4, bit_extender_1_out, controlled_buffer_1_out, DeviceID, multiplexer_1_out, PC,
       ram_1_data, ram_2_data, register_1_q, register_2_q;
  wire [31:24] register_3_q_2;

  Clock clock_1 (.out(CLK));
  Register #(.width(32)) u_PC (.D(controlled_buffer_1_out), .en(LdPC), .Q(PC), .clk(CLK));  // open: clr
  Multiplexer #(.width(32), .disabled(0), .enable("false")) multiplexer_1 (
    .in0(PC), .in1(32'h10), .out(multiplexer_1_out), .sel(Start));
  assign controlled_buffer_1_out = DrPC ? multiplexer_1_out : 32'bz;  // Controlled_Buffer controlled_buffer_1
  Comparator #(.width(32)) comparator_1 (
    .a(controlled_buffer_1_out), .b({32{1'b0}}), .gt(comparator_1_gt[0]), .eq(comparator_1_gt[1]),
    .lt(comparator_1_gt[2]));
  and and_1 (and_1_out, IR[22], N);
  and and_2 (and_2_out, IR[21], Z);
  or or_1 (or_1_out, and_1_out, and_2_out, and_3_out);
  Register #(.width(3)) CC (.D(comparator_1_gt), .en(LdCC), .Q({N, Z, P}), .clk(CLK));  // open: clr
  and and_3 (and_3_out, IR[20], P);
  Register #(.width(32)) register_1 (.D(controlled_buffer_1_out), .en(LdA), .Q(register_1_q), .clk(CLK));  // open: clr
  ALU alu_1 (.A(register_1_q), .B(register_2_q), .func(func), .out_4(alu_1_out_4));
  assign controlled_buffer_1_out = DrALU ? alu_1_out_4 : 32'bz;  // Controlled_Buffer controlled_buffer_2
  Register #(.width(32)) register_2 (.D(controlled_buffer_1_out), .en(LdB), .Q(register_2_q), .clk(CLK));  // open: clr
  RAM #(.addrWidth(4), .dataWidth(32), .bus("separate")) ram_1 (
    .addr(regno), .din(controlled_buffer_1_out), .data(ram_1_data), .str(WrREG), .clk(CLK));  // open: sel, ld, clr
  assign controlled_buffer_1_out = DrREG ? ram_1_data : 32'bz;  // Controlled_Buffer controlled_buffer_3
  Control_Unit control_unit_1 (
    .CCMatch(or_1_out), .IR({out_1, IR}), .regno(regno), .CLK(CLK), .DrREG(DrREG), .DrMEM(DrMEM),
    .DrALU(DrALU), .DrPC(DrPC), .DrOFF(DrOFF), .LdPC(LdPC), .LdIR(LdIR), .LdMAR(LdMAR), .LdA(LdA), .LdB(LdB),
    .LdCC(LdCC), .WrREG(WrREG), .WrMEM(WrMEM), .LdEnInt(LdEnInt), .ALU(func), .EnInt(EnInt), .IntAck(IntAck),
    .in_4(INT));
  Register #(.width(32)) register_3 (
    .D(controlled_buffer_1_out), .en(LdMAR), .Q({register_3_q_2, register_3_q}), .clk(CLK));  // open: clr
  RAM #(.addrWidth(24), .dataWidth(32), .bus("separate")) ram_2 (
    .addr(register_3_q), .din(controlled_buffer_1_out), .data(ram_2_data), .str(WrMEM), .clk(CLK));  // open: sel, ld, clr
  assign controlled_buffer_1_out = DrMEM ? ram_2_data : 32'bz;  // Controlled_Buffer controlled_buffer_4
  Register #(.width(32)) u_IR (.D(controlled_buffer_1_out), .en(LdIR), .Q({out_1, IR}), .clk(CLK));  // open: clr
  assign controlled_buffer_1_out = DrOFF ? bit_extender_1_out : 32'bz;  // Controlled_Buffer controlled_buffer_5
  assign controlled_buffer_1_out = IntAck ? DeviceID : 32'bz;  // Controlled_Buffer controlled_buffer_6
  and and_4 (INT, Interrupt, IE);
  assign bit_extender_1_out = {{12{IR[19]}}, IR[19:0]};  // Bit_Extender bit_extender_1
  Intergenerator intergenerator_1 (.CLK(CLK), .IntAck(IntAck), .IntOut(IntOut), .DeviceID(DeviceID));
  Register #(.width(1)) register_4 (.D(IntOut), .en(IE), .Q(Interrupt), .clk(CLK), .clr(IntAck));
  Comparator #(.width(32), .mode("unsigned")) comparator_2 (.a(PC), .b(32'h10), .lt(Start));  // open: gt, eq
  Register #(.width(1)) register_5 (.D(EnInt), .en(LdEnInt), .Q(IE), .clk(CLK));  // open: clr

  // Other names for the same wires on the sheet: p_t = IR[20]; z_t = IR[21]; n_t = IR[22]; IR[31:28] = out_1

  // Notes on the sheet:
  //   CheckCC
endmodule

// ALU:32
module ALU (
  input  [31:0] A,
  input  [31:0] B,
  input  [1:0] func,
  output [31:0] out_4
);

  wire [31:0] adder_1_out, adder_2_out, nand_1_out;

  Adder #(.width(32)) adder_1 (.a(A), .b(B), .out(adder_1_out));  // open: cin, cout
  assign nand_1_out = ~(A & B);  // NAND_Gate nand_1, 32 bits wide
  Multiplexer #(.select(2), .width(32), .disabled(0), .enable("false")) multiplexer_1 (
    .in0(adder_1_out), .in1(nand_1_out), .in2(adder_2_out), .out(out_4), .sel(func));  // open: in3
  Adder #(.width(32)) adder_2 (.a(A), .b(32'h1), .out(adder_2_out));  // open: cin, cout

  // Notes on the sheet:
  //   The 32-bit ALU
endmodule

module Control_Unit (
  input  CCMatch,
  input  [31:0] IR,
  input  CLK,
  input  in_4,
  output DrREG,
  output DrMEM,
  output DrALU,
  output DrPC,
  output DrOFF,
  output LdPC,
  output LdIR,
  output LdMAR,
  output LdA,
  output LdB,
  output LdCC,
  output WrREG,
  output WrMEM,
  output [1:0] ALU,
  output LdEnInt,
  output EnInt,
  output IntAck,
  output [3:0] regno
);

  wire chkCC, OPTest, or_1_out;
  wire [1:0] RegSel;
  wire [5:0] multiplexer_1_out, rom_1_data, rom_2_data, rom_3_data, rom_4_data, State_q;
  wire [17:17] rom_1_data_2;

  Register #(.width(6)) State (.D(multiplexer_1_out), .en(1'b1), .Q(State_q), .clk(CLK));  // open: clr
  ROM #(.addrWidth(6), .dataWidth(28)) rom_1 (
    .addr(State_q),
    .data({IntAck, EnInt, LdEnInt, chkCC, OPTest, ALU, RegSel, WrMEM, rom_1_data_2[17], LdCC, LdB, LdA, LdMAR, LdIR, LdPC, DrOFF, DrPC, DrALU, DrMEM, DrREG, rom_1_data}));  // open: sel
  Multiplexer #(.select(2), .width(6), .disabled(0), .enable("false")) multiplexer_1 (
    .in0(rom_1_data), .in1(rom_2_data), .in2(rom_3_data), .in3(rom_4_data), .out(multiplexer_1_out),
    .sel({chkCC, OPTest}));
  ROM #(.addrWidth(4), .dataWidth(6)) rom_2 (.addr(IR[31:28]), .data(rom_2_data));  // open: sel
  ROM #(.addrWidth(2), .dataWidth(6)) rom_3 (.addr({1'b0, CCMatch}), .data(rom_3_data));  // open: sel
  ROM #(.addrWidth(2), .dataWidth(6)) rom_4 (.addr({1'b0, in_4}), .data(rom_4_data));  // open: sel
  or or_1 (or_1_out, regno[0], regno[1], regno[2], regno[3]);
  Multiplexer #(.select(2), .width(4), .disabled(0), .enable("false")) multiplexer_2 (
    .in0(IR[27:24]), .in1(IR[23:20]), .in2(IR[3:0]), .in3(4'b1100), .out(regno), .sel(RegSel));
  and and_1 (WrREG, or_1_out, rom_1_data_2[17]);

  // Other names for the same wires on the sheet: INT = in_4

  // Notes on the sheet:
  //   Inputs
  //   Primary State ROM
  //   contents of rom_1 (hex, n*v repeats v):
  //   1800001 6202 1083 400909 0 21a0206 8002007 880 0 800000 0 8404c 10804d 30100 8404f 8410 30100 84052
  //   108053 230100 1000000 8216 4417 900 20219 80840 8405b 841c 211d 30080 8405f 8420 2121 40040 6000000
  //   2000000 6180840 25 8427 4228 30100
  //   IR[15..13] ROM
  //   CCMatch ROM
  //   contents of rom_2 (hex, n*v repeats v):
  //   b e 11 14 18 1a 26 1e 22 23 24 4*0 25
  //   contents of rom_3 (hex, n*v repeats v):
  //   1 15
  //   contents of rom_4 (hex, n*v repeats v):
  //   1 5
  //   Zero Reigster Write Lock
endmodule

module Intergenerator (
  input  CLK,
  input  IntAck,
  output IntOut,
  output [31:0] DeviceID
);

  wire comparator_1_eq;
  wire [9:0] adder_1_out, register_1_q;

  Adder #(.width(10)) adder_1 (.a(10'h1), .b(register_1_q), .out(adder_1_out));  // open: cin, cout
  Register #(.width(10)) register_1 (.D(adder_1_out), .en(1'b1), .Q(register_1_q), .clk(CLK));  // open: clr
  Comparator #(.width(10), .mode("unsigned")) comparator_1 (
    .a({10{1'b1}}), .b(register_1_q), .eq(comparator_1_eq));  // open: gt, lt
  Register #(.width(1)) register_2 (.D(comparator_1_eq), .en(comparator_1_eq), .Q(IntOut), .clk(CLK), .clr(IntAck));

  assign DeviceID = 32'h1;
endmodule
