// Logisim project LC3-2200a.circ as structural Verilog: 4 circuits, main circuit my circuit
module my_circuit (
  output [3:0] out_1
);

  wire ALUHi, ALULo, cc_1_n, cc_1_p, cc_1_z, CCMatch, CLK, comparator_1_eq, comparator_1_gt, comparator_1_lt,
       comparator_2_eq, DrALU, DrMEM, DrOFF, DrPC, DrREG, LdA, LdB, LdCC, LdIR, LdMAR, LdPC, n, p, RegSelHi,
       RegSelLo, WrMEM, WrREG;
  wire [3:0] Regno, Rx;
  wire [3:1] Ry;
  wire [5:0] multiplexer_3_out, register_4_q, rom_2_data, rom_3_data;
  wire [19:0] IR_19_0;
  wire [23:0] register_5_q;
  wire [24:0] rom_1_data;
  wire [31:0] alu_1_out_4, bit_extender_1_out, bit_extender_2_out, controlled_buffer_1_out,
       multiplexer_2_out, ram_1_data, ram_2_data, register_1_q, register_2_q, register_3_q;

  Register #(.width(32)) register_1 (.D(controlled_buffer_1_out), .en(LdPC), .Q(register_1_q), .clk(CLK));  // open: clr
  Register #(.width(32)) register_2 (.D(controlled_buffer_1_out), .en(LdA), .Q(register_2_q), .clk(CLK));  // open: clr
  assign controlled_buffer_1_out = DrPC ? register_1_q : 32'bz;  // Controlled_Buffer controlled_buffer_1
  Comparator #(.width(32)) comparator_1 (
    .a(controlled_buffer_1_out), .b({32{1'b0}}), .gt(comparator_1_gt), .eq(comparator_1_eq),
    .lt(comparator_1_lt));
  Clock clock_1 (.out(CLK));
  Register #(.width(32)) register_3 (.D(controlled_buffer_1_out), .en(LdB), .Q(register_3_q), .clk(CLK));  // open: clr
  ALU alu_1 (.in_1(register_2_q), .in_2(register_3_q), .out_4(alu_1_out_4), .FUNC({ALUHi, ALULo}));
  assign controlled_buffer_1_out = DrALU ? alu_1_out_4 : 32'bz;  // Controlled_Buffer controlled_buffer_2
  Multiplexer #(.select(2), .width(4), .disabled(0), .enable("false")) multiplexer_1 (
    .in0(Rx), .in1({Ry[3], n, Ry[1], p}), .in2(IR_19_0[3:0]), .out(Regno), .sel({RegSelHi, RegSelLo}));  // open: in3
  CC cc_1 (
    .Pi(comparator_1_gt), .Zi(comparator_1_eq), .Ni(comparator_1_lt), .LdCC(LdCC), .CLK(CLK), .P(cc_1_p),
    .Z(cc_1_z), .N(cc_1_n));
  Comparator #(.width(4)) comparator_2 (.a(Regno), .b(4'b0000), .eq(comparator_2_eq));  // open: gt, lt
  CCMatch ccmatch_1 (.p(cc_1_p), .P_2(p), .z(cc_1_z), .Z_2(Ry[1]), .n(cc_1_n), .N_2(n), .out_7(CCMatch));
  RAM #(.addrWidth(4), .dataWidth(32), .bus("separate")) ram_1 (
    .addr(Regno), .din(controlled_buffer_1_out), .data(ram_1_data), .str(WrREG), .clk(CLK));  // open: sel, ld, clr
  assign bit_extender_1_out = {{28{Regno[3]}}, Regno};  // Bit_Extender bit_extender_1
  Multiplexer #(.width(32), .enable("false")) multiplexer_2 (
    .in0(ram_1_data), .in1(bit_extender_1_out), .out(multiplexer_2_out), .sel(comparator_2_eq));
  assign controlled_buffer_1_out = DrREG ? multiplexer_2_out : 32'bz;  // Controlled_Buffer controlled_buffer_3
  ROM #(.addrWidth(6), .dataWidth(25)) rom_1 (
    .addr(register_4_q),
    .data({rom_1_data[24:23], ALUHi, ALULo, RegSelHi, RegSelLo, WrMEM, WrREG, LdCC, LdB, LdA, LdMAR, LdIR, LdPC, DrOFF, DrPC, DrALU, DrMEM, DrREG, rom_1_data[5:0]}));  // open: sel
  Register #(.width(6)) register_4 (.D(multiplexer_3_out), .Q(register_4_q), .clk(CLK));  // open: en, clr
  Register #(.width(24)) register_5 (
    .D(controlled_buffer_1_out[23:0]), .en(LdMAR), .Q(register_5_q), .clk(CLK));  // open: clr
  Multiplexer #(.select(2), .width(6), .disabled(0), .enable("false")) multiplexer_3 (
    .in0(rom_1_data[5:0]), .in1(rom_2_data), .in2(rom_3_data), .out(multiplexer_3_out),
    .sel(rom_1_data[24:23]));  // open: in3
  RAM #(.addrWidth(24), .dataWidth(32), .bus("separate")) ram_2 (
    .addr(register_5_q), .din(controlled_buffer_1_out), .data(ram_2_data), .str(WrMEM), .clk(CLK));  // open: sel, ld, clr
  assign controlled_buffer_1_out = DrMEM ? ram_2_data : 32'bz;  // Controlled_Buffer controlled_buffer_4
  Register #(.width(32)) register_6 (
    .D(controlled_buffer_1_out), .en(LdIR), .Q({out_1, Rx, Ry[3], n, Ry[1], p, IR_19_0}), .clk(CLK));  // open: clr
  assign bit_extender_2_out = {{12{IR_19_0[19]}}, IR_19_0};  // Bit_Extender bit_extender_2
  assign controlled_buffer_1_out = DrOFF ? bit_extender_2_out : 32'bz;  // Controlled_Buffer controlled_buffer_5
  ROM #(.addrWidth(4), .dataWidth(6)) rom_2 (.addr(out_1), .data(rom_2_data));  // open: sel
  ROM #(.addrWidth(2), .dataWidth(6)) rom_3 (.addr({1'b0, CCMatch}), .data(rom_3_data));  // open: sel

  // Other names for the same wires on the sheet: Rz[3:0] = IR_19_0[3:0]; Ry (some bits) = {n, p}; z = Ry[1];
  //   OPCODE[3:0] = out_1

  // Notes on the sheet:
  //   contents of rom_1 (hex, n*v repeats v):
  //   6201 1082 400903 800000 0 84046 108047 30100 0 8404a 840b 30100 0 8404e 10804f 230100 0 1000000 8213
  //   4414 900 0 20217 80840 0 8405a 841b 211c 30080 0 841f 4220 30100 0 84063 8424 2125 40040 0 27
  //   Ankit Khanal
  //   903093845
  //   contents of rom_2 (hex, n*v repeats v):
  //   5 9 d 11 16 19 1e 22 7*0 27
  //   contents of rom_3 (hex, n*v repeats v):
  //   0 12
endmodule

module ALU (
  input  [31:0] in_1,
  input  [31:0] in_2,
  input  [1:0] FUNC,
  output [31:0] out_4
);

  wire [31:0] A_1, ADD, NAND;

  Adder #(.width(32)) adder_1 (.a(in_1), .b(in_2), .out(ADD));  // open: cin, cout
  assign NAND = ~(in_1 & in_2);  // NAND_Gate nand_1, 32 bits wide
  Multiplexer #(.select(2), .width(32), .enable("false")) multiplexer_1 (
    .in0(ADD), .in1(NAND), .in2(A_1), .out(out_4), .sel(FUNC));  // open: in3
  Adder #(.width(32)) adder_2 (.a(in_1), .b(32'h1), .out(A_1));  // open: cin, cout

  // Other names for the same wires on the sheet: A[31:0] = in_1; B[31:0] = in_2; Out[31:0] = out_4

  // Notes on the sheet:
  //   00 - ADD
  //   01 - NAND
  //   10 - A+1
endmodule

module CCMatch (
  input  p,
  input  P_2,
  input  z,
  input  Z_2,
  input  n,
  input  N_2,
  output out_7
);

  wire and_1_out, and_2_out, and_3_out;

  and and_1 (and_1_out, p, P_2);
  and and_2 (and_2_out, z, Z_2);
  and and_3 (and_3_out, n, N_2);
  or or_1 (out_7, and_1_out, and_2_out, and_3_out);
endmodule

module CC (
  input  Pi,
  input  Zi,
  input  Ni,
  input  LdCC,
  input  CLK,
  output P,
  output Z,
  output N
);

  Register #(.width(1)) u_P (.D(Pi), .en(LdCC), .Q(P), .clk(CLK));  // open: clr
  Register #(.width(1)) u_Z (.D(Zi), .en(LdCC), .Q(Z), .clk(CLK));  // open: clr
  Register #(.width(1)) u_N (.D(Ni), .en(LdCC), .Q(N), .clk(CLK));  // open: clr
endmodule
